# Fritzing sketch traffic-light-controller (saved by Fritzing 0.9.3b)

parts:
  U1 = NodeMCU V3.0
  LED4 = LEDs [package=led10mm]
  Power_plug1 = Power plug
  LED5 = LEDs [package=led10mm]
  U3 = TRANSFORMER VB 1,5/1/9 [part_number="VB 1,5/1/9" package=transformer]
  U2 = TRANSFORMER VB 1,5/1/9 [part_number="VB 1,5/1/9" package=transformer]
  DHT2 = Humidity and Temperature Sensor DHT11
  DHT3 = Humidity and Temperature Sensor DHT11
  R1 = Resistor [tolerance=±5% resistance=10k package=THT]
  R2 = Resistor [tolerance=±5% resistance=10k package=THT]
  Part2 = Solid State High Level Relay Module [package=relay]
  Part3 = Solid State High Level Relay Module [package=relay]

nets:
  N1: U1.D3, DHT3.Data-signal, R2.Pin_0
  N2: U1.D4, DHT2.Data-signal, R1.Pin_0
  VCC: U1.3V3, DHT2.Vcc, DHT3.Vcc, R1.Pin_1, R2.Pin_1
  N3: U1.GND#6, U1.GND#33, DHT2.GND_2, Part2.DC-, Part3.DC-
  N4: U1.D5, Part3.CH1
  N5: U1.D6, Part2.CH1
  N6: U1.VU, Part2.DC+, Part3.DC+
  N7: U1.GND#41, DHT3.GND_2
  N8: LED4.A, U2.3
  N9: LED4.C, U2.4
  N10: Power_plug1.VCC, U3.1, U2.1
  N11: Power_plug1.GND, Part2.A1, Part3.A1
  N12: LED5.A, U3.3
  N13: LED5.C, U3.4
  N14: U3.2, Part3.B1
  N15: U2.2, Part2.B1

notes:
  AC 220V
  AC 10.5V
  GREEN light
  RED light
  GREEN temperature sensor
  RED temperature sensor

custom parts:
  NodeMCU V3.0: ESP8266 based NodeMCU
  LEDs: LEDs Standard schematic elements and footprints for 5mm, 3mm, 1206, and 0603 sized LEDs. 5mm - Spark Fun Electronics SKU : COM-00529 (and others)
  TRANSFORMER VB 1,5/1/9: VB 1,5/1/9 Short circuit proof PCB transformer
  Humidity and Temperature Sensor DHT11: Digital relative humidity & temperature sensor DHT11
  Solid State High Level Relay Module: 5V Omron solid state relay 240V 2A output with resistance fuse.
