# Fritzing sketch traffic-light-board (saved by Fritzing 0.9.3b)
perfboards: 2

parts:
  J2 = male pin header, 4 pins [form="♂ (male)"]
  J1 = female pin header, 15 pins [form="♀ (female)"]
  J3 = female pin header, 15 pins [form="♀ (female)"]
  U2 = NodeMCU V3.0
  J4 = male pin header, 3 pins [form="♂ (male)"]
  R2 = Resistor [tolerance=±5% resistance=10k package=THT]
  DHT3 = Humidity and Temperature Sensor DHT11
  J5 = female pin header, 3 pins [form="♀ (female)"]
  J6 = female pin header, 3 pins [form="♀ (female)"]

nets:
  N1: J2.pin1, J1.pin14
  N2: J2.pin2, J3.pin8
  N3: J2.pin3, J3.pin7
  N4: J2.pin4, J1.pin13
  N5: J1.pin2, J6.pin1
  N6: J1.pin5, J6.pin3
  N7: J3.pin1, J5.pin3
  N8: J3.pin2, J5.pin1
  N9: J3.pin11, J5.pin2
  N10: J3.pin12, J6.pin2
  N11: U2.GND#6, U2.GND#13, U2.GND#16, U2.GND#33
  N12: J4.pin1, R2.Pin_1, DHT3.Vcc
  N13: J4.pin2, R2.Pin_0, DHT3.Data-signal
  N14: J4.pin3, DHT3.GND_2

notes:
  D6 D5
  VU GND
  GND
  D5
  D6
  VU
  SIG
  VCC
  to RED sensor
  to GREEN sensor
  DHT11 adapter board (2x)
  VCC SIG GND
  to RELAY

custom parts:
  NodeMCU V3.0: ESP8266 based NodeMCU
  Humidity and Temperature Sensor DHT11: Digital relative humidity & temperature sensor DHT11
