# Fritzing sketch traffic-light-controller (saved by Fritzing 0.9.3b)

parts:
  U1 = NodeMCU V3.0
  2_Channel_Relay2 = richardbruneau00
  LED4 = LEDs [package=led10mm]
  Power_plug1 = Power plug
  J2 = Thyristor AC swith - 2 channel dimmer [form="♂ (male)" package=THT]
  LED5 = LEDs [package=led10mm]
  J3 = Thyristor AC swith - 2 channel dimmer [form="♂ (male)" package=THT]
  U2 = TRANSFORMER VB 1,5/1/9 [part_number="VB 1,5/1/9" package=transformer]
  U3 = TRANSFORMER VB 1,5/1/9 [part_number="VB 1,5/1/9" package=transformer]

nets:
  N1: U1.D1, J2.L1
  N2: U1.D2, J3.L1
  N3: U1.D3, 2_Channel_Relay2.connector12
  N4: U1.D4, 2_Channel_Relay2.connector13
  N5: U1.3V3, 2_Channel_Relay2.connector14
  GND: U1.GND#6, U1.GND#13, U1.GND#16, J2.GND, J3.GND
  N6: U1.GND#41, 2_Channel_Relay2.connector11
  N7: 2_Channel_Relay2.connector16, 2_Channel_Relay2.connector19, Power_plug1.VCC
  N8: 2_Channel_Relay2.connector17, J2.L_-_IN
  N9: 2_Channel_Relay2.connector20, J3.L_-_IN
  N10: LED4.A, U2.3
  N11: LED4.C, U2.4
  N12: Power_plug1.GND, J2.N_-_IN, J3.N_-_IN
  N13: J2.L1_-_OUT, U2.1
  N14: J2.N1_-_OUT, U2.2
  N15: LED5.A, U3.3
  N16: LED5.C, U3.4
  N17: J3.L1_-_OUT, U3.1
  N18: J3.N1_-_OUT, U3.2

custom parts:
  NodeMCU V3.0: ESP8266 based NodeMCU
  LEDs: LEDs Standard schematic elements and footprints for 5mm, 3mm, 1206, and 0603 sized LEDs. 5mm - Spark Fun Electronics SKU : COM-00529 (and others)
  Thyristor AC swith - 2 channel dimmer: Robodyn 2 channel dimmer
  TRANSFORMER VB 1,5/1/9: VB 1,5/1/9 Short circuit proof PCB transformer
